# Fritzing sketch connections (saved by Fritzing 0.9.9b)

parts:
  Mod2 = ESP32-TTGO-T-DISPLAY
  TD-er1 = MH-Z19 CO2 sensor [part_number=MH-Z19]

nets:
  N1: Mod2.G-11, Mod2.G-14, TD-er1.GND
  5V: Mod2.5V, TD-er1.Vin
  N2: Mod2.25, TD-er1.RX
  N3: Mod2.33, TD-er1.TX

custom parts:
  ESP32-TTGO-T-DISPLAY: LILYGO TTGO T-Display GD32VF103CBT6 Main Chip ST7789 1.14 Inch IPS 240x135 Resolution Minimalist Development Board.
